# Fritzing sketch circuit (saved by Fritzing 0.9.3b)
breadboards: 1

parts:
  Onderdeel1 = Arduino Nano (Rev3.0) (ICSP)
  Onderdeel2 = Real Time Clock Module - DS1307 RTC Breakout Board
  GY1 = GY-5150 (MPU-9150) [form="♀ (female)" package=THT]
  VCC1 = Battery block 9V

nets:
  GND: Onderdeel1.GND, Onderdeel2.GND, GY1.pin2, VCC1.-
  N1: Onderdeel1.VIN, VCC1.+
  5V: Onderdeel1.5V, Onderdeel2.5V
  N2: Onderdeel1.A5, Onderdeel2.SCL, GY1.pin3
  N3: Onderdeel1.A4, Onderdeel2.SDA, GY1.pin4
  N4: Onderdeel1.3V3, GY1.pin1, GY1.pin7

custom parts:
  GY-5150 (MPU-9150): Placa GY-5150 basada en conjunto de acelerómetro+giroscopios+magnetómetro MPU-9150
